# Fritzing sketch design (saved by Fritzing 0.9.3b)

parts:
  Raspberry_Pi_1 = Raspberry Pi 3 [part_number=RPI-3-V1.2]  # not connected
  Matrix_keypad1 = KEYPAD 4x4
  Part1 = RFID-RC522-v2
  Part2 = Arduino Mega ADK (Rev3)
  J2 = Piezo Speaker
  Part3 = Thermal Printer
  J1 = Power Jack [package=power_jack_pth_lock]
  M2 = Stepper Motor - Unipolar
  M3 = Stepper Motor - Unipolar
  M4 = Stepper Motor - Unipolar
  M5 = Stepper Motor - Unipolar
  driver = X113647 Stepper Driver Board [package=board]
  driver_2 = X113647 Stepper Driver Board [package=board]
  driver_3 = X113647 Stepper Driver Board [package=board]
  driver_4 = X113647 Stepper Driver Board [package=board]

nets:
  N1: Matrix_keypad1.col1, Part2.D22
  N2: Matrix_keypad1.col2, Part2.D23
  N3: Matrix_keypad1.col3, Part2.D24
  N4: Matrix_keypad1.col4, Part2.D25
  N5: Matrix_keypad1.row1, Part2.D26
  N6: Matrix_keypad1.row2, Part2.D27
  N7: Matrix_keypad1.row3, Part2.D28
  N8: Matrix_keypad1.row4, Part2.D29
  N9: Part1.SDA, Part2.D53/SS
  N10: Part1.SCK, Part2.D52/SCK
  N11: Part1.MOSI, Part2.D51/MOSI
  N12: Part1.MISO, Part2.D50/MISO
  GND: Part1.GND, Part2.GND, J2.pin1
  N13: Part1.RST, Part2.D49
  3.3V: Part1.3.3V, Part2.5V
  N14: Part2.D19/RX1, Part3.TXD
  N15: Part2.D18/TX1, Part3.RXD
  N16: Part2.D2_PWM, J2.pin2
  N17: Part2.D30, driver.IN1
  N18: Part2.D31, driver.IN2
  N19: Part2.D32, driver.IN3
  N20: Part2.D33, driver.IN4
  N21: Part2.D34, driver_2.IN1
  N22: Part2.D35, driver_2.IN2
  N23: Part2.D36, driver_2.IN3
  N24: Part2.D37, driver_2.IN4
  N25: Part2.D38, driver_3.IN1
  N26: Part2.D39, driver_3.IN2
  N27: Part2.D40, driver_3.IN3
  N28: Part2.D41, driver_3.IN4
  N29: Part2.D42, driver_4.IN1
  N30: Part2.D43, driver_4.IN2
  N31: Part2.D44, driver_4.IN3
  N32: Part2.D45, driver_4.IN4
  GND_2: Part3.GND#0, driver.GND, driver_2.GND, driver_3.GND, driver_4.GND
  N33: Part3.VH, J1.PWR, driver.+V, driver_2.+V, driver_3.+V, driver_4.+V
  N34: Part3.GND#2, J1.GNDBREAK
  N35: M2.A, driver.PINK
  N36: M2.COMMON_1, M2.COMMON_2, driver.RED
  N37: M2.C, driver.ORANGE
  N38: M2.B, driver.YELLOW
  N39: M2.D, driver.BLUE
  N40: M3.A, driver_2.PINK
  N41: M3.COMMON_1, M3.COMMON_2, driver_2.RED
  N42: M3.C, driver_2.ORANGE
  N43: M3.B, driver_2.YELLOW
  N44: M3.D, driver_2.BLUE
  N45: M4.A, driver_3.PINK
  N46: M4.COMMON_1, M4.COMMON_2, driver_3.RED
  N47: M4.C, driver_3.ORANGE
  N48: M4.B, driver_3.YELLOW
  N49: M4.D, driver_3.BLUE
  N50: M5.A, driver_4.PINK
  N51: M5.COMMON_1, M5.COMMON_2, driver_4.RED
  N52: M5.C, driver_4.ORANGE
  N53: M5.B, driver_4.YELLOW
  N54: M5.D, driver_4.BLUE

notes:
  Money dispenser is comming soon...
  Arduino Mega USB Raspberry Pi

custom parts:
  KEYPAD 4x4: Matrix keypad 16 buttons, 4 rows x 4 columns
  RFID-RC522-v2: A simple China made RFID-RC522 Reader; do check the pin labels, as this is a MFRC522 based clone.
  X113647 Stepper Driver Board: A common stepper motor driver board based on ULN2003APG darlington array
