# Fritzing sketch test-controller-design (saved by Fritzing 0.9.3b)

parts:
  Arduino_Uno = Arduino Uno (Rev3) - ICSP
  RFID_Reader = RFID-RC522-v2
  Keypad = KEYPAD 4x4
  Beeper = Piezo Speaker

nets:
  N1: Arduino_Uno.A0, RFID_Reader.SDA
  N2: Arduino_Uno.A1, RFID_Reader.GND
  N3: Arduino_Uno.GND, Beeper.pin2
  5V: Arduino_Uno.5V, RFID_Reader.3.3V
  N4: Arduino_Uno.D8, Keypad.row2
  N5: Arduino_Uno.D9_PWM, Keypad.row3
  N6: Arduino_Uno.D10_PWM/SS, Keypad.row4
  N7: Arduino_Uno.D11_PWM/MOSI, RFID_Reader.MOSI
  N8: Arduino_Uno.D12/MISO, RFID_Reader.MISO
  N9: Arduino_Uno.D13/SCK, RFID_Reader.SCK
  N10: Arduino_Uno.D2, Beeper.pin1
  N11: Arduino_Uno.D3_PWM, Keypad.col1
  N12: Arduino_Uno.D4, Keypad.col2
  N13: Arduino_Uno.D5_PWM, Keypad.col3
  N14: Arduino_Uno.D6_PWM, Keypad.col4
  N15: Arduino_Uno.D7, Keypad.row1

custom parts:
  RFID-RC522-v2: A simple China made RFID-RC522 Reader; do check the pin labels, as this is a MFRC522 based clone.
  KEYPAD 4x4: Matrix keypad 16 buttons, 4 rows x 4 columns
