# Fritzing sketch design (saved by Fritzing 0.9.3b)
breadboards: 1

parts:
  U1 = NodeMCU V1.0
  Part1 = RFID-RC522-v2
  Matrix_keypad1 = KEYPAD 4x4  # not connected

nets (from the schematic view):
  GND: U1.D3, U1.GND, Part1.GND
  N1: U1.D4, Part1.SDA
  3V3: U1.3V3, Part1.3.3V
  N2: U1.D5, Part1.SCK
  N3: U1.D6, Part1.MISO
  N4: U1.D7, Part1.MOSI

custom parts:
  NodeMCU V1.0: ESP8266 based NodeMCU
  RFID-RC522-v2: A simple China made RFID-RC522 Reader; do check the pin labels, as this is a MFRC522 based clone.
  KEYPAD 4x4: Matrix keypad 16 buttons, 4 rows x 4 columns
